# Fritzing sketch Scheme (saved by Fritzing 0.9.2b)

parts:
  Part1 = Arduino Uno (Rev3)
  J5 = Basic Servo
  J6 = Basic Servo
  J7 = Basic Servo
  J8 = Basic Servo

nets:
  N1: Part1.D9_PWM, J6.pulse
  N2: Part1.D10_PWM/SS, J7.pulse
  N3: Part1.D11_PWM/MOSI, J8.pulse
  N4: Part1.D6_PWM, J5.pulse
  VCC: Part1.5V, J5.vcc, J6.vcc, J7.vcc, J8.vcc
  GND: Part1.GND, J5.gnd, J6.gnd, J7.gnd, J8.gnd
